# Fritzing sketch Schéma patate (saved by Fritzing 0.9.3b)
breadboards: 1

parts:
  Composant1 = Arduino Uno (Rev3)
  R1 = Resistor [tolerance=±5% resistance=1M package=THT]
  L1 = Inductor [package="400 mil [THT]"]
  R2 = Resistor [tolerance=±5% resistance=100 package=THT]
  LED1 = LED - 5mm [color="Red (633nm)" package="5 mm [THT]"]
  R3 = Resistor [tolerance=±5% resistance=18 package=THT]
  LED2 = LED - 5mm [color="Yellow (574nm)" package="5 mm [THT]"]
  R4 = Resistor [tolerance=±5% resistance=15 package=THT]
  R5 = Resistor [tolerance=±5% resistance=15 package=THT]
  LED3 = LED - 5mm [color="Green (570nm)" package="5 mm [THT]"]

nets:
  Patate: Composant1.A0, L1.pin_1, R2.Pin_0
  N1: Composant1.D9_PWM, R2.Pin_1
  N2: Composant1.GND, R1.Pin_0, LED1.cathode, LED2.cathode, LED3.cathode
  N3: Composant1.D3_PWM, R3.Pin_1
  N4: Composant1.D5_PWM, R4.Pin_1
  N5: Composant1.D7, R5.Pin_1
  N6: R1.Pin_1, L1.pin_0
  N7: LED1.anode, R3.Pin_0
  N8: LED2.anode, R4.Pin_0
  N9: R5.Pin_0, LED3.anode
